# Fritzing sketch esp32_and_scd30_co2_sensor_circuit_diagram (saved by Fritzing 0.9.3b)

parts:
  esp1 = ESP32 DevKitc V4
  Part1 = Adafruit SCD30 [part_number="Adafruit #4867"]

nets:
  N1: esp1.IO21, Part1.SDA
  N2: esp1.IO22, Part1.SCL
  GND: esp1.GND, Part1.GND
  3V3: esp1.3V3, Part1.VCC

custom parts:
  ESP32 DevKitc V4: ESP32-DevKitC board with ESP32-WROOM-32 module. ESP32-DevKitC V4 is a small-sized ESP32-based development board produced by Espressif. Most of the pins on the ESP module are broken out to the pin headers on the board. The pins D0, D1, D2, D3, CMD and CLK are used internally for communication between ESP32 and SPI flash memory. They are grouped on both sides near the USB connector. Avoid using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
