# Fritzing sketch ublox_neo_m8n_gps_with_esp32 (saved by Fritzing 1.0.1rc)

parts:
  esp1 = ESP32 DevKitc V4
  M1 = NEO-M8N GPS Module [part_number=GY-GPSV3-NEO]

nets:
  N1: esp1.IO16, M1.Tx
  N2: esp1.IO17, M1.Rx
  GND: esp1.GND, M1.GND
  5V: esp1.5V, M1.Vcc

custom parts:
  ESP32 DevKitc V4: ESP32-DevKitC board with ESP32-WROOM-32 module. ESP32-DevKitC V4 is a small-sized ESP32-based development board produced by Espressif. Most of the pins on the ESP module are broken out to the pin headers on the board. The pins D0, D1, D2, D3, CMD and CLK are used internally for communication between ESP32 and SPI flash memory. They are grouped on both sides near the USB connector. Avoid using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
  NEO-M8N GPS Module: GY-GPSV3-NEO NEO-M8N GPS Module Module based on U-blox NEO-M8N GPS engine, incorporating regulator for 3.3-5V DC input, MS621FE-compatible rechargeable battery for backup and EEPROM for storing configuration settings. Links: NEO-M8 series Product Summary NEO-M8 Datasheet
